# Fritzing sketch camara (saved by Fritzing 0.9.3b)
breadboards: 1

parts:
  Componente1 = Arduino Uno (Rev3)
  DRFGSDXGCV = Resistor [tolerance=±5% resistance=220 package=THT]
  R1 = Resistor [tolerance=±5% resistance=220 package=THT]
  R2 = Resistor [tolerance=±5% resistance=220 package=THT]
  R3 = Resistor [tolerance=±5% resistance=220 package=THT]

nets:
  N1: Componente1.A4/SDA, R1.Pin_1
  N2: Componente1.A5/SCL, DRFGSDXGCV.Pin_0
  N3: Componente1.D11_PWM/MOSI, R2.Pin_0, R3.Pin_0, R3.Pin_1
  N4: Componente1.GND, R2.Pin_1
  N5: Componente1.3V3, DRFGSDXGCV.Pin_1, R1.Pin_0

notes:
  3v3
  GND
  SIOC
  SIOD
  VSYNC
  PCLK
  XCLK
  D7
  D6
  D5
  D4
  D3
  D2
  D1
  RESET
  PWDN
