# Fritzing sketch starwarstheme (saved by Fritzing 0.9.3b)
breadboards: 1

parts:
  S1 = Pushbutton [package="[SMD]"]
  R1 = Resistor [tolerance=±5% resistance=220 package=THT]
  LED1 = LED - 5mm [color="Red (633nm)" package="5 mm [THT]"]
  R2 = Resistor [tolerance=±5% resistance=220 package=THT]
  Componente1 = Arduino Uno (Rev3)
  J1 = Piezo Speaker

nets:
  N1: S1.Pin_1, S1.Pin_2, R1.Pin_1, Componente1.D2
  N2: S1.Pin_3, S1.Pin_4
  N3: R1.Pin_0, R2.Pin_1, Componente1.GND, J1.pin1
  N4: LED1.cathode, Componente1.D6_PWM
  N5: LED1.anode, R2.Pin_0
  N6: Componente1.D9_PWM, J1.pin2
