# Fritzing sketch parpadeoLED (saved by Fritzing 0.9.3b)
breadboards: 1

parts:
  Componente1 = Arduino Uno (Rev3)
  LED1 = LED - 5mm [color="Red (633nm)" package="5 mm [THT]"]
  R1 = Resistor [tolerance=±5% resistance=220 package=THT]

nets:
  N1: Componente1.GND, R1.Pin_1
  N2: Componente1.D2, LED1.cathode
  N3: LED1.anode, R1.Pin_0
