# Fritzing sketch pulsadorLED (saved by Fritzing 0.9.3b)
breadboards: 1

parts:
  S1 = Pushbutton [package="[THT]"]
  Componente1 = Arduino Uno (Rev3)
  R1 = Resistor [tolerance=±5% resistance=220 package=THT]
  LED1 = LED - 5mm [color="Red (633nm)" package="5 mm [THT]"]
  R2 = Resistor [tolerance=±5% resistance=220 package=THT]

nets:
  N1: S1.Pin_1, S1.Pin_2, Componente1.D2, R1.Pin_0
  N2: S1.Pin_3, S1.Pin_4, Componente1.5V
  N3: Componente1.D3_PWM, LED1.cathode
  N4: Componente1.GND, R1.Pin_1, R2.Pin_0
  N5: LED1.anode, R2.Pin_1
