# Fritzing sketch sensorLuz (saved by Fritzing 0.9.3b)
breadboards: 1

parts:
  Componente1 = Arduino Uno (Rev3)
  R1 = PHOTOCELL [package=photocell]
  R2 = Resistor [tolerance=±5% resistance=220 package=THT]
  R3 = Resistor [tolerance=±5% resistance=220 package=THT]
  LED1 = LED - 5mm [color="Red (633nm)" package="5 mm [THT]"]
  J1 = Piezo Speaker

nets:
  N1: Componente1.A0, R1.P$1, R2.Pin_1
  N2: Componente1.D12/MISO, J1.pin2
  N3: Componente1.D13/SCK, R3.Pin_0
  N4: Componente1.5V, R1.P$2
  N5: Componente1.GND, R2.Pin_0, R3.Pin_1, LED1.cathode
